# Fritzing sketch biruta nova (saved by Fritzing 0.9.3b)
breadboards: 1

parts:
  part = Resistor [tolerance=±5% resistance=10k package=THT]
  S1 = Pushbutton [package=THT]
  S2 = Pushbutton [package=THT]
  S3 = Pushbutton [package=THT]
  S4 = Pushbutton [package=THT]
  S5 = Pushbutton [package=THT]
  S6 = Pushbutton [package=THT]
  S7 = Pushbutton [package=THT]
  S8 = Pushbutton [package=THT]
  part_2 = Resistor [tolerance=±5% resistance=10k package=THT]
  part_3 = Resistor [tolerance=±5% resistance=10k package=THT]
  part_4 = Resistor [tolerance=±5% resistance=10k package=THT]
  part_5 = Resistor [tolerance=±5% resistance=10k package=THT]
  part_6 = Resistor [tolerance=±5% resistance=10k package=THT]
  part_7 = Resistor [tolerance=±5% resistance=10k package=THT]
  part_8 = Resistor [tolerance=±5% resistance=10k package=THT]
  part_9 = Resistor [tolerance=±5% resistance=10k package=THT]
  part_10 = Resistor [tolerance=±5% resistance=10k package=THT]

nets:
  GND: part.Pin_1, part_10.Pin_0
  N1: S1.leg0, part_2.Pin_0, part_7.Pin_1
  3.3V: S1.leg1, S2.leg1, S3.leg1, S4.leg1, S5.leg1, S6.leg1, S7.leg1, S8.leg1
  N2: S2.leg0, part_2.Pin_1, part_5.Pin_0
  N3: S3.leg0, part_4.Pin_0, part_6.Pin_1
  N4: S4.leg0, part_6.Pin_0, part_9.Pin_1
  N5: S5.leg0, part_7.Pin_0, part_8.Pin_1
  N6: S6.leg0, part_3.Pin_0, part_4.Pin_1
  N7: S7.leg0, part_3.Pin_1, part_8.Pin_0
  N8: S8.leg0, part_9.Pin_0
  analog01: part_5.Pin_1, part_10.Pin_1
