# Fritzing sketch biruta (saved by Fritzing 0.9.3b)
breadboards: 1

parts:
  R1 = Resistor [tolerance=±5% resistance=4.7k package=THT]
  S1 = Pushbutton [package=THT]
  R2 = Resistor [tolerance=±5% resistance=220 package=THT]
  S2 = Pushbutton [package=THT]
  R3 = Resistor [tolerance=±5% resistance=220 package=THT]
  S3 = Pushbutton [package=THT]
  part = Resistor [tolerance=±5% resistance=220 package=THT]
  S4 = Pushbutton [package=THT]
  part_2 = Resistor [tolerance=±5% resistance=220 package=THT]
  S5 = Pushbutton [package=THT]
  R6 = Resistor [tolerance=±5% resistance=220 package=THT]
  S6 = Pushbutton [package=THT]
  S7 = Pushbutton [package=THT]
  R8 = Resistor [tolerance=±5% resistance=220 package=THT]
  S8 = Pushbutton [package=THT]
  R9 = Resistor [tolerance=±5% resistance=220 package=THT]
  R7 = Resistor [tolerance=±5% resistance=220 package=THT]

nets:
  analog01: R1.Pin_0, S1.leg0, S2.leg0, S3.leg0, S4.leg0, S5.leg0, S6.leg0, S7.leg0, S8.leg0
  GND: R1.Pin_1
  N1: S1.leg1, R2.Pin_0
  3.3V: R2.Pin_1, R3.Pin_1, part.Pin_1, part_2.Pin_1, R6.Pin_1, R8.Pin_0, R9.Pin_1, R7.Pin_1
  N2: S2.leg1, R3.Pin_0
  N3: S3.leg1, part.Pin_0
  N4: S4.leg1, part_2.Pin_0
  N5: S5.leg1, R6.Pin_0
  N6: S6.leg1, R7.Pin_0
  N7: S7.leg1, R8.Pin_1
  N8: S8.leg1, R9.Pin_0
