# Fritzing sketch dht22 (saved by Fritzing 0.9.3b)
breadboards: 1

parts:
  DHT22 = DHT22 Humidity and Temperature Sensor
  part = Resistor [tolerance=±5% resistance=10k package=THT]

nets:
  3.3V: DHT22.VDD, part.Pin_1
  digital02: DHT22.DATA, part.Pin_0
  GND: DHT22.GND
