# Fritzing sketch nodemcu v2 (saved by Fritzing 0.9.3b)
breadboards: 1

parts:
  ESP8266 = NodeMCU V1.0
  part = Resistor [tolerance=±5% resistance=10k package=THT]
  Reset_WiFi = Pushbutton [package=THT]
  part_2 = Resistor [tolerance=±5% resistance=10k package=THT]
  part_3 = Resistor [tolerance=±5% resistance=10k package=THT]
  part_4 = Resistor [tolerance=±5% resistance=10k package=THT]
  DHT1 = DHT22 Humidity and Temperature Sensor
  part_5 = Resistor [tolerance=±5% resistance=10k package=THT]

nets (from the schematic view):
  anem. (out): ESP8266.D1, part_3.Pin_0
  pluv (out): ESP8266.D3, part_4.Pin_0
  N1: ESP8266.D4, DHT1.DATA, part_5.Pin_1
  3.3V/biruta (in): ESP8266.3V3, part.Pin_0, part_3.Pin_1, part_4.Pin_1, DHT1.VDD, part_5.Pin_0
  GND/anem. (in)/pluv. (in): ESP8266.GND, Reset_WiFi.leg0, part_2.Pin_0, DHT1.GND
  6V: ESP8266.Vin
  N2: ESP8266.SD3, part.Pin_1, Reset_WiFi.leg1
  biruta (out): ESP8266.A0, part_2.Pin_1

custom parts:
  NodeMCU V1.0: ESP8266 based NodeMCU
