# Fritzing sketch nodemcu (saved by Fritzing 0.9.3b)
breadboards: 1

parts:
  ESP8266 = NodeMCU V1.0

nets:
  digital01 (anemometro): ESP8266.D1
  digital03 (pluviometro): ESP8266.D2
  digital02 (temperatura): ESP8266.D4
  GND: ESP8266.GND
  3.3V: ESP8266.3V3
  6V: ESP8266.Vin
  analog01 (biruta): ESP8266.A0

custom parts:
  NodeMCU V1.0: ESP8266 based NodeMCU
