# Fritzing sketch pluviometro (saved by Fritzing 0.9.3b)
breadboards: 1

parts:
  part = Resistor [tolerance=±5% resistance=10k package=THT]
  reed_switch = Reed switch [package=THT]

nets:
  3.3V: part.Pin_0
  digital03: part.Pin_1, reed_switch.pin_2
  GND: reed_switch.pin_1
